# Fritzing sketch Tipsy_Schematic (saved by Fritzing 0.9.2b)
stripboards: 4

parts:
  Part1 = Motor Driver 1A Dual TB6612FNG  # not connected
  VCC1 = Battery  # not connected
  VCC2 = Battery
  IC1 = Voltage Regulator [package=to-220-alt]
  J3 = female pin header, 2 pins [form="♀ (female)"]
  J4 = female pin header, 2 pins [form="♀ (female)"]  # not connected
  J5 = female pin header, 2 pins [form="♀ (female)"]  # not connected
  J6 = female pin header, 2 pins [form="♀ (female)"]  # not connected
  J7 = female pin header, 2 pins [form="♀ (female)"]  # not connected
  J8 = female pin header, 2 pins [form="♀ (female)"]  # not connected
  J9 = female pin header, 2 pins [form="♀ (female)"]  # not connected
  J10 = female pin header, 2 pins [form="♀ (female)"]  # not connected
  R1 = Trimmer Potentiometer [maximum_resistance=10kΩ package=THT]  # not connected
  R2 = Trimmer Potentiometer [maximum_resistance=10kΩ package=THT]  # not connected
  R3 = Trimmer Potentiometer [maximum_resistance=10kΩ package=THT]  # not connected
  M1 = DC Motor  # not connected
  M2 = DC Motor  # not connected

nets:
  N1: VCC2.-, IC1.IN, IC1.OUT, J3.pin2

notes:
  1
  5
  10
  15
  20
  30
  25
  50
  40
  35
  44
  55
  67
  65
  60
  45
  a     b     c     d     e
  f     g     h     i     j
  + -
  >5v RAIL
  5v RAIL
  VCC
  PORTC
  Rx6
  Rx2
  Rx4
  Rx0
  Rx1
  GND
  Rx3
  Rx5
  Rx7
  MOSI
  SCLK
  CS
  MISO
  FSNC
  ADA
  INT
  VIN
  4
  6
  2
  3
  0
  7
  VPP
  RX
  TX
  PIN1: VPP
  PIN2: VCC
  PIN3: GND
  PIN4: RB7
  PIN6: NOT USED
  PIN5: RB6
  A01
  VM
  A02
  B01
  B02
  AI1
  AI2
  STBY
  PWMA
  BI1
  PWMB
  BI2
  MOTOR B
  MOTOR A
  Note for motors:
  Schematic Color Yellow = Red Lead
  Schematic Color Green = Black Lead
  Note that I2C side of chip is shown in picture, labels are for SPI side of chip (on back side). You can orient yourself via GND and VIN pins
  Note - If needed, I can use MSSP1 from the PIC18F87K22 dev board to test the IMU with the LCD. Per 12-5 of PIC18F87K22 data sheet
  RC3 = SCK1
  RC4 = SDI1 (Master In)
  RC5 = SDO1 (Master Out)
  and we will use RC2 as CS
  We will also connect the ground to the tipsy bot so we have a common ground
  PIC18F87K22
  IMU to PIC Cheatsheet
  IMU PIC
  MOSI (DA) Rx
  SCLK (CL) RB1
  MISO (AD0) RB0
  CS (NC) RB2
